# Fritzing sketch smart_street_light (saved by Fritzing 0.9.3b)
breadboards: 1

parts:
  Part1 = Arduino Uno (Rev3)
  LED1 = LEDs [package=led10mm]
  LED2 = LEDs [package=led10mm]
  LED3 = LEDs [package=led10mm]
  LED4 = LEDs [package=led10mm]
  LED5 = LEDs [package=led10mm]
  LED6 = LEDs [package=led10mm]
  M1 = fc-51 [package=THT]
  M2 = fc-51 [package=THT]
  M3 = fc-51 [package=THT]
  M4 = fc-51 [package=THT]

nets:
  N1: Part1.D8, LED3.A
  N2: Part1.D9_PWM, LED4.A
  N3: Part1.D10_PWM/SS, LED5.A
  N4: Part1.D11_PWM/MOSI, LED6.A
  N5: Part1.GND, LED5.C, M1.pin3, M2.pin3, M3.pin3, M4.pin3
  N6: Part1.D2, M2.pin1
  N7: Part1.D3_PWM, M4.pin1
  N8: Part1.D4, M3.pin1
  N9: Part1.D5_PWM, M1.pin1
  N10: Part1.D6_PWM, LED1.A
  N11: Part1.D7, LED2.A
  N12: Part1.5V, M1.pin2, M2.pin2, M3.pin2, M4.pin2
